# Fritzing sketch Button (saved by Fritzing 0.9.8b)
breadboards: 1

parts:
  Mod1 = Raspberry Pi Pico
  S1 = Tactile Switch Buttons - 12mm Square [package=tactile-pth-12mm]
  LED1 = LEDs [package=led10mm]

nets:
  N1: Mod1.pin_1, S1.1, S1.3
  N2: Mod1.pin_2, LED1.A
  N3: Mod1.pin_3, Mod1.pin_8, Mod1.pin_13, Mod1.pin_18, Mod1.pin_23, Mod1.pin_28, Mod1.pin_33, Mod1.pin_38, Mod1.pin_42, S1.2, S1.4, LED1.C

notes:
  Button Press/Blink
  GPIO 0 - Button
  GPIO 1 - Led + (long side)
  GND - LED -
  Power - 3.3v
  Ground - Any gnd pin

custom parts:
  Raspberry Pi Pico: Raspberry Pi Pico. Based around the RP2040 microcontroller the Pico is a low cost microcontroller device bringing Raspberry Pi quality, cost, and easy of use to the microcontroller space. Jan 2021, Split part in to two versions: tht (this one) and SMD. This one will drill holes for a .1 in header in pcb to allow plugging in the module as well as providing pads to solder the module to the top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
  Tactile Switch Buttons - 12mm Square: Medium-sized clicky momentary switches are standard input "buttons" on electronic projects. These work best in a PCB but can be used on a solderless breadboard as shown in this tutorial. The pins are normally open (disconnected) and when the button is pressed they are momentarily closed. They come in a pack of 10, they're pretty handy so you'll want to keep them around. You can find an EAGLE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
