# Fritzing sketch neopixel_game (saved by Fritzing 1.0.1rc)
breadboards: 1

parts:
  Mod1 = Raspberry Pi Pico
  OLED_I2C1 = OLED 128x64 I2C Monochrome Display
  S1 = Tactile Switch Buttons - 12mm Square [package=tactile-pth-12mm]
  Part1 = 12 NeoPixel Ring [part_number=1643]

nets:
  N1: Mod1.pin_1, Part1.IN
  N2: Mod1.pin_2, S1.1, S1.3
  GND: Mod1.pin_3, Mod1.pin_8, Mod1.pin_13, Mod1.pin_18, Mod1.pin_23, Mod1.pin_28, Mod1.pin_33, Mod1.pin_38, Mod1.pin_42, OLED_I2C1.GND, S1.2, S1.4, Part1.GND
  N3: Mod1.pin_19, OLED_I2C1.SDA
  N4: Mod1.pin_20, OLED_I2C1.SCK
  VDD: Mod1.pin_36, OLED_I2C1.VDD, Part1.VDD

notes:
  Light Game
  GPIO 15 - LCD SDA
  GPIO 14 - LCD SDC
  GPIO 1 - Push Button
  GPIO 0 - Neopixel data
  Power - 3.3v
  Ground - Any gnd pin

custom parts:
  Raspberry Pi Pico: Raspberry Pi Pico. Based around the RP2040 microcontroller the Pico is a low cost microcontroller device bringing Raspberry Pi quality, cost, and easy of use to the microcontroller space. Jan 2021, Split part in to two versions: tht (this one) and SMD. This one will drill holes for a .1 in header in pcb to allow plugging in the module as well as providing pads to solder the module to the top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
  Tactile Switch Buttons - 12mm Square: Medium-sized clicky momentary switches are standard input "buttons" on electronic projects. These work best in a PCB but can be used on a solderless breadboard as shown in this tutorial. The pins are normally open (disconnected) and when the button is pressed they are momentarily closed. They come in a pack of 10, they're pretty handy so you'll want to keep them around. You can find an EAGLE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
  12 NeoPixel Ring: 12 ultra bright smart LED NeoPixels are arranged in a circle with 1.5" (37mm) outer diameter. The rings are 'chainable' - connect the output pin of one to the input pin of another. Use only one microcontroller pin to control as many as you can chain together! Each LED is addressable as the driver chip is inside the LED. Each one has ~18mA constant current drive so the color will be very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
